// Logisim project Bidirectional_Shift_Register.circ as structural Verilog: 1 circuit, main circuit main
module main (
  input  LOAD,
  input  LEFT_SHIFT,
  input  RIGHT_SHIFT
);

  wire and_1_out, and_2_out, and_3_out, and_4_out, and_5_out, and_6_out, and_7_out, and_8_out, CLK_out,
       CLR_out, d_ff_1_q, d_ff_2_q, d_ff_3_q, d_ff_4_q, not_1_out, or_1_out, or_2_out, or_3_out, or_4_out;

  Clock CLK (.out(CLK_out));
  Button CLR (.out(CLR_out));
  not not_1 (not_1_out, LOAD);
  and and_1 (and_1_out, RIGHT_SHIFT, LOAD);
  or or_1 (or_1_out, and_1_out, and_2_out);
  and and_2 (and_2_out, not_1_out, d_ff_2_q);
  D_Flip_Flop d_ff_1 (.D(or_1_out), .clk(CLK_out), .Q(d_ff_1_q), .reset(CLR_out));  // open: Qn, preset
  and and_3 (and_3_out, d_ff_1_q, LOAD);
  LED led_1 (.in(d_ff_1_q));
  and and_4 (and_4_out, not_1_out, d_ff_3_q);
  or or_2 (or_2_out, and_3_out, and_4_out);
  D_Flip_Flop d_ff_2 (.D(or_2_out), .clk(CLK_out), .Q(d_ff_2_q), .reset(CLR_out));  // open: Qn, preset
  and and_5 (and_5_out, d_ff_2_q, LOAD);
  and and_6 (and_6_out, not_1_out, d_ff_4_q);
  or or_3 (or_3_out, and_5_out, and_6_out);
  D_Flip_Flop d_ff_3 (.D(or_3_out), .clk(CLK_out), .Q(d_ff_3_q), .reset(CLR_out));  // open: Qn, preset
  and and_7 (and_7_out, d_ff_3_q, LOAD);
  or or_4 (or_4_out, and_7_out, and_8_out);
  and and_8 (and_8_out, not_1_out, LEFT_SHIFT);
  D_Flip_Flop d_ff_4 (.D(or_4_out), .clk(CLK_out), .Q(d_ff_4_q), .reset(CLR_out));  // open: Qn, preset
  LED led_2 (.in(d_ff_4_q));

  // Notes on the sheet:
  //   4 Bit Biderectional Shift Register
endmodule
