// Logisim project PIPO.circ as structural Verilog: 1 circuit, main circuit main
module main (
  input  PA,
  input  PB,
  input  PC,
  input  PD,
  input  PE,
  input  PF,
  input  PG,
  input  PH
);

  wire CLK_out, CLR_out, d_ff_1_q, d_ff_2_q, d_ff_3_q, d_ff_4_q, d_ff_5_q, d_ff_6_q, d_ff_7_q, d_ff_8_q;

  Clock CLK (.out(CLK_out));
  Button CLR (.out(CLR_out));
  D_Flip_Flop d_ff_1 (.D(PA), .clk(CLK_out), .Q(d_ff_1_q), .Qn(CLR_out));  // open: preset, reset
  LED led_1 (.in(d_ff_1_q));
  D_Flip_Flop d_ff_2 (.D(PB), .clk(CLK_out), .Q(d_ff_2_q), .Qn(CLR_out));  // open: preset, reset
  D_Flip_Flop d_ff_3 (.D(PC), .clk(CLK_out), .Q(d_ff_3_q), .Qn(CLR_out));  // open: preset, reset
  LED led_2 (.in(d_ff_2_q));
  LED led_3 (.in(d_ff_3_q));
  D_Flip_Flop d_ff_4 (.D(PD), .clk(CLK_out), .Q(d_ff_4_q), .Qn(CLR_out));  // open: preset, reset
  LED led_4 (.in(d_ff_4_q));
  D_Flip_Flop d_ff_5 (.D(PE), .clk(CLK_out), .Q(d_ff_5_q), .Qn(CLR_out));  // open: preset, reset
  D_Flip_Flop d_ff_6 (.D(PF), .clk(CLK_out), .Q(d_ff_6_q), .Qn(CLR_out));  // open: preset, reset
  LED led_5 (.in(d_ff_5_q));
  LED led_6 (.in(d_ff_6_q));
  D_Flip_Flop d_ff_7 (.D(PG), .clk(CLK_out), .Q(d_ff_7_q), .Qn(CLR_out));  // open: preset, reset
  D_Flip_Flop d_ff_8 (.D(PH), .clk(CLK_out), .Q(d_ff_8_q), .Qn(CLR_out));  // open: preset, reset
  LED led_7 (.in(d_ff_7_q));
  LED led_8 (.in(d_ff_8_q));

  // Notes on the sheet:
  //   MSB
  //   8-Bit Parallel Out Shift Register (PIPO)
  //   Bit 1
  //   Bit 2
  //   Bit 3
  //   Bit 4
  //   Bit 5
  //   Bit 6
  //   Bit 7
  //   LSB
  //   Bit 8
endmodule
