// Logisim project PISO.circ as structural Verilog: 1 circuit, main circuit main
module main (
  input  Q1,
  input  Q2,
  input  Q3,
  input  Q4,
  input  Q5,
  input  Q6,
  input  Q7,
  input  Q8,
  input  Q9,
  input  SHIFT_LOAD
);

  wire and_1_out, and_2_out, and_3_out, and_4_out, and_5_out, and_6_out, and_7_out, and_8_out, and_9_out,
       and_10_out, and_11_out, and_12_out, and_13_out, and_14_out, and_15_out, and_16_out, button_1_out,
       clock_1_out, d_ff_1_q, d_ff_2_q, d_ff_3_q, d_ff_4_q, d_ff_5_q, d_ff_6_q, d_ff_7_q, d_ff_8_q, d_ff_9_q,
       not_1_out, or_1_out, or_2_out, or_3_out, or_4_out, or_5_out, or_6_out, or_7_out, or_8_out;

  Clock clock_1 (.out(clock_1_out));
  Button button_1 (.out(button_1_out));
  not not_1 (not_1_out, SHIFT_LOAD);
  D_Flip_Flop d_ff_1 (.D(Q1), .clk(clock_1_out), .Q(d_ff_1_q), .reset(button_1_out));  // open: Qn, preset
  and and_1 (and_1_out, d_ff_1_q, SHIFT_LOAD);
  LED led_1 (.in(d_ff_1_q));
  and and_2 (and_2_out, not_1_out, Q2);
  or or_1 (or_1_out, and_1_out, and_2_out);
  D_Flip_Flop d_ff_2 (.D(or_1_out), .clk(clock_1_out), .Q(d_ff_2_q), .reset(button_1_out));  // open: Qn, preset
  LED led_2 (.in(d_ff_2_q));
  and and_3 (and_3_out, d_ff_2_q, SHIFT_LOAD);
  or or_2 (or_2_out, and_3_out, and_4_out);
  D_Flip_Flop d_ff_3 (.D(or_2_out), .clk(clock_1_out), .Q(d_ff_3_q), .reset(button_1_out));  // open: Qn, preset
  and and_4 (and_4_out, not_1_out, Q3);
  and and_5 (and_5_out, d_ff_3_q, SHIFT_LOAD);
  or or_3 (or_3_out, and_5_out, and_6_out);
  LED led_3 (.in(d_ff_3_q));
  and and_6 (and_6_out, not_1_out, Q4);
  D_Flip_Flop d_ff_4 (.D(or_3_out), .clk(clock_1_out), .Q(d_ff_4_q), .reset(button_1_out));  // open: Qn, preset
  and and_7 (and_7_out, d_ff_4_q, SHIFT_LOAD);
  or or_4 (or_4_out, and_7_out, and_8_out);
  LED led_4 (.in(d_ff_4_q));
  and and_8 (and_8_out, not_1_out, Q5);
  D_Flip_Flop d_ff_5 (.D(or_4_out), .clk(clock_1_out), .Q(d_ff_5_q), .reset(button_1_out));  // open: Qn, preset
  and and_9 (and_9_out, d_ff_5_q, SHIFT_LOAD);
  or or_5 (or_5_out, and_9_out, and_10_out);
  LED led_5 (.in(d_ff_5_q));
  and and_10 (and_10_out, not_1_out, Q6);
  D_Flip_Flop d_ff_6 (.D(or_5_out), .clk(clock_1_out), .Q(d_ff_6_q), .reset(button_1_out));  // open: Qn, preset
  and and_11 (and_11_out, d_ff_6_q, SHIFT_LOAD);
  LED led_6 (.in(d_ff_6_q));
  and and_12 (and_12_out, not_1_out, Q7);
  or or_6 (or_6_out, and_11_out, and_12_out);
  D_Flip_Flop d_ff_7 (.D(or_6_out), .clk(clock_1_out), .Q(d_ff_7_q), .reset(button_1_out));  // open: Qn, preset
  and and_13 (and_13_out, d_ff_7_q, SHIFT_LOAD);
  LED led_7 (.in(d_ff_7_q));
  and and_14 (and_14_out, not_1_out, Q8);
  or or_7 (or_7_out, and_13_out, and_14_out);
  D_Flip_Flop d_ff_8 (.D(or_7_out), .clk(clock_1_out), .Q(d_ff_8_q), .reset(button_1_out));  // open: Qn, preset
  and and_15 (and_15_out, d_ff_8_q, SHIFT_LOAD);
  LED led_8 (.in(d_ff_8_q));
  and and_16 (and_16_out, not_1_out, Q9);
  or or_8 (or_8_out, and_15_out, and_16_out);
  D_Flip_Flop d_ff_9 (.D(or_8_out), .clk(clock_1_out), .Q(d_ff_9_q), .reset(button_1_out));  // open: Qn, preset
  LED led_9 (.in(d_ff_9_q));

  // Notes on the sheet:
  //   DATA MASUK
  //   CLOCK
  //   RESET
  //   MSB
  //   Bit 1
  //   9-Bit Parallel In Serial Shift Register (PISO)
  //   Bit 2
  //   Bit 3
  //   Bit 4
  //   Bit 5
  //   Bit 6
  //   Bit 7
  //   Bit 8
  //   LSB
  //   Bit 9
endmodule
