// Logisim project SIPO.circ as structural Verilog: 1 circuit, main circuit main
module main (
  input  X,
  input  Y
);

  wire and_1_out, CLK_out, CLR_out, d_ff_1_q, d_ff_2_q, d_ff_3_q, d_ff_4_q, d_ff_5_q, d_ff_6_q, d_ff_7_q,
       d_ff_8_q, d_ff_9_q, not_1_out;

  Clock CLK (.out(CLK_out));
  LED CPLED (.in(CLK_out));
  Button CLR (.out(CLR_out));
  and and_1 (and_1_out, X, Y);
  not not_1 (not_1_out, CLK_out);
  D_Flip_Flop d_ff_1 (.D(and_1_out), .clk(not_1_out), .Q(d_ff_1_q), .Qn(CLR_out));  // open: preset, reset
  LED Q1 (.in(d_ff_1_q));
  D_Flip_Flop d_ff_2 (.D(d_ff_1_q), .clk(not_1_out), .Q(d_ff_2_q), .Qn(CLR_out));  // open: preset, reset
  D_Flip_Flop d_ff_3 (.D(d_ff_2_q), .clk(not_1_out), .Q(d_ff_3_q), .Qn(CLR_out));  // open: preset, reset
  LED Q2 (.in(d_ff_2_q));
  LED Q3 (.in(d_ff_3_q));
  D_Flip_Flop d_ff_4 (.D(d_ff_3_q), .clk(not_1_out), .Q(d_ff_4_q), .Qn(CLR_out));  // open: preset, reset
  D_Flip_Flop d_ff_5 (.D(d_ff_4_q), .clk(not_1_out), .Q(d_ff_5_q), .Qn(CLR_out));  // open: preset, reset
  LED Q4 (.in(d_ff_4_q));
  LED Q5 (.in(d_ff_5_q));
  D_Flip_Flop d_ff_6 (.D(d_ff_5_q), .clk(not_1_out), .Q(d_ff_6_q), .Qn(CLR_out));  // open: preset, reset
  D_Flip_Flop d_ff_7 (.D(d_ff_6_q), .clk(not_1_out), .Q(d_ff_7_q), .Qn(CLR_out));  // open: preset, reset
  LED Q6 (.in(d_ff_6_q));
  LED Q7 (.in(d_ff_7_q));
  D_Flip_Flop d_ff_8 (.D(d_ff_7_q), .clk(not_1_out), .Q(d_ff_8_q), .Qn(CLR_out));  // open: preset, reset
  D_Flip_Flop d_ff_9 (.D(d_ff_8_q), .clk(not_1_out), .Q(d_ff_9_q), .Qn(CLR_out));  // open: preset, reset
  LED Q8 (.in(d_ff_8_q));
  LED Q9 (.in(d_ff_9_q));

  // Notes on the sheet:
  //   9 Bit Serial In Parallel Out Shift Register
  //   Data Masuk Serial
  //   AND
  //   MSB
  //   Data Keluar Parallel
  //   LSB
endmodule
