// Logisim project Universal_Shift_Register.circ as structural Verilog: 1 circuit, main circuit main
module main (
  input  Shift_Right,
  input  I4,
  input  I3,
  input  I2,
  input  Shift_Left,
  input  I1,
  input  [1:0] Select_Bits
);

  wire button_1_out, clock_1_out, d_ff_1_q, d_ff_2_q, d_ff_3_q, d_ff_4_q, multiplexer_1_out,
       multiplexer_2_out, multiplexer_3_out, multiplexer_4_out;

  Multiplexer #(.select(2)) multiplexer_1 (
    .in0(d_ff_1_q), .in1(Shift_Right), .in2(d_ff_2_q), .in3(I4), .out(multiplexer_1_out), .sel(Select_Bits));
  Multiplexer #(.select(2)) multiplexer_2 (
    .in0(d_ff_2_q), .in1(d_ff_1_q), .in2(d_ff_3_q), .in3(I3), .out(multiplexer_2_out), .sel(Select_Bits));
  Multiplexer #(.select(2)) multiplexer_3 (
    .in0(d_ff_3_q), .in1(d_ff_2_q), .in2(d_ff_4_q), .in3(I2), .out(multiplexer_3_out), .sel(Select_Bits));
  Multiplexer #(.select(2)) multiplexer_4 (
    .in0(d_ff_4_q), .in1(d_ff_3_q), .in2(Shift_Left), .in3(I1), .out(multiplexer_4_out), .sel(Select_Bits));
  Clock clock_1 (.out(clock_1_out));
  D_Flip_Flop d_ff_1 (
    .D(multiplexer_1_out), .clk(clock_1_out), .Q(d_ff_1_q), .reset(button_1_out));  // open: Qn, preset
  D_Flip_Flop d_ff_2 (
    .D(multiplexer_2_out), .clk(clock_1_out), .Q(d_ff_2_q), .reset(button_1_out));  // open: Qn, preset
  D_Flip_Flop d_ff_3 (
    .D(multiplexer_3_out), .clk(clock_1_out), .Q(d_ff_3_q), .reset(button_1_out));  // open: Qn, preset
  D_Flip_Flop d_ff_4 (
    .D(multiplexer_4_out), .clk(clock_1_out), .Q(d_ff_4_q), .reset(button_1_out));  // open: Qn, preset
  LED A4 (.in(d_ff_1_q));
  LED A3 (.in(d_ff_2_q));
  LED A2 (.in(d_ff_3_q));
  LED A1 (.in(d_ff_4_q));
  Button button_1 (.out(button_1_out));

  // Notes on the sheet:
  //   4 BIT  UNIVERSAL SHIFT REGISTER
  //   CLK
  //   CLR
endmodule
